# Fritzing sketch schematic (saved by Fritzing 0.9.3b)
breadboards: 1

parts:
  Raspberry_Pi_1 = Raspberry Pi 3 [part_number=RPI-3-V1.2]  # not connected
  Part1 = Adafruit Pi Cobbler [part_number="Adafruit #914"]
  R1 = Resistor [tolerance=±0.05% resistance=4.7k package="0603 [SMD]"]
  DS1 = DS18B20 1-Wire Temperature Sensor Probe Cable

nets:
  GND: Part1.GND, DS1.GND
  3.3V: Part1.3.3V, R1.Pin_0, DS1.DQ, DS1.VDD
  N1: Part1.GPIO4, R1.Pin_1, DS1.shield

custom parts:
  Adafruit Pi Cobbler: Now that you've finally got your hands on a Raspberry Pi® Model B , you're probably itching to make some fun embedded computer projects with it. What you need is an add on prototyping Pi Cobbler from Adafruit, which can break out all those tasty power, GPIO, I2C and SPI pins from the 26 pin header onto a solderless breadboard. This set will make "cobbling together" prototypes with the Pi super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
